# Fritzing sketch Spark.Core.MPL115A2 (saved by Fritzing 0.9.1b)
circuit board: 8.46667cm x 5.64444cm
breadboards: 1

parts:
  Spark_io_Core = Spark Core (v1.0)
  DHT22 = Humidity and Temperature Sensor RHT03
  MPL115A2 = MPL3115A2 [package=lga8]
  R1 = Resistor [tolerance=±5% resistance=10k package=THT]
  R2 = Resistor [tolerance=±5% resistance=10k package=THT]
  R3 = Resistor [tolerance=±5% resistance=10k package=THT]
  Photo_Resistor = PHOTOCELL [package=photocell]
  R5 = Resistor [tolerance=±5% resistance=10k package="1206 [SMD]"]

nets (from the schematic view):
  N1: Spark_io_Core.A0, Photo_Resistor.P$1, R5.Pin_1
  GND: Spark_io_Core.GND, DHT22.GND_2, MPL115A2.GND, R5.Pin_0
  N2: Spark_io_Core.D0, MPL115A2.SDA, R2.Pin_1
  N3: Spark_io_Core.D1, MPL115A2.SCL, R1.Pin_1
  N4: Spark_io_Core.D4, DHT22.Data-signal, R3.Pin_1
  3V3: Spark_io_Core.3V3, DHT22.Vcc, MPL115A2.VDD, R1.Pin_0, R2.Pin_0, Photo_Resistor.P$2
